# Fritzing sketch dino-wiring (saved by Fritzing 0.9.10b)
breadboards: 1

parts:
  LCD1 = LCD screen
  R1 = Resistor [tolerance=±5% resistance=4700 package="0603 [SMD]"]
  R4 = Trimmer Potentiometer [maximum_resistance=10kΩ knob_status=50% power=0.5W package=THT]
  M1 = Raspberry Pi Pico

nets:
  N1: LCD1.VSS, R1.Pin_1, R4.leg2, M1.pin_3, M1.pin_8, M1.pin_13, M1.pin_18, M1.pin_23, M1.pin_28, M1.pin_33, M1.pin_38, M1.pin_42
  N2: LCD1.VDD, LCD1.LED+, R4.leg1, M1.pin_40
  N3: LCD1.V0, R1.Pin_0
  N4: LCD1.RS, M1.pin_20
  N5: LCD1.R/W, M1.pin_19
  N6: LCD1.E, M1.pin_17
  N7: LCD1.DB0, M1.pin_16
  N8: LCD1.DB1, M1.pin_15
  N9: LCD1.DB2, M1.pin_14
  N10: LCD1.DB3, M1.pin_12
  N11: LCD1.DB4, M1.pin_11
  N12: LCD1.DB5, M1.pin_10
  N13: LCD1.DB6, M1.pin_9
  N14: LCD1.DB7, M1.pin_7
  N15: LCD1.LED-, R4.wiper

custom parts:
  Raspberry Pi Pico: Raspberry Pi Pico. Based around the RP2040 microcontroller the Pico is a low cost microcontroller device bringing Raspberry Pi quality, cost, and easy of use to the microcontroller space. Jan 2021, Split part in to two versions: SMD (this one) and tht. This one is single sided and uses the castellation pads to solder the module to the board (no holes, other than for the USB connector!). The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
